# Fritzing sketch Tray_Iter_1 (saved by Fritzing 0.9.3b)
breadboards: 1

parts:
  S1 = Pushbutton [package="[THT]"]
  S2 = Pushbutton [package="[THT]"]
  S3 = Pushbutton [package="[THT]"]
  R1 = Resistor [tolerance=±5% resistance=1k package=THT]
  R2 = Resistor [tolerance=±5% resistance=1k package=THT]
  R3 = Resistor [tolerance=±5% resistance=1k package=THT]
  R4 = Resistor [tolerance=±5% resistance=1k package=THT]
  R5 = Resistor [tolerance=±5% resistance=2k package=THT]
  S4 = Pushbutton [package="[THT]"]
  Part2 = Adafruit Pro Trinket 5V 16MHz [part_number="Adafruit #2000"]
  DS1 = DS18B20 1-Wire Temperature Sensor Probe Cable
  NEOPIXEL1 = Neopixel Strip -- Black (30/m) [part_number=1376]
  S5 = Pushbutton [package="[THT]"]
  R6 = Resistor [tolerance=±5% resistance=4.7 package="0402 [SMD]"]

nets:
  GND: S1.Pin_1, S1.Pin_2, S2.Pin_1, S2.Pin_2, S3.Pin_1, S3.Pin_2, S4.Pin_1, S4.Pin_2, Part2.GND, DS1.GND, NEOPIXEL1.GND, S5.Pin_3, S5.Pin_4
  N1: S1.Pin_3, S1.Pin_4, R1.Pin_0
  N2: S2.Pin_3, S2.Pin_4, R1.Pin_1, R2.Pin_0
  N3: S3.Pin_3, S3.Pin_4, R2.Pin_1, R3.Pin_0
  N4: R3.Pin_1, R4.Pin_0, S4.Pin_3, S4.Pin_4
  N5: R4.Pin_1, R5.Pin_0, Part2.A0
  VDD: R5.Pin_1, DS1.VDD, NEOPIXEL1.+5V, R6.Pin_1
  N6: Part2.D6, NEOPIXEL1.Din
  N7: Part2.D10, DS1.DQ, R6.Pin_0
  N8: Part2.D11, S5.Pin_2

custom parts:
  Adafruit Pro Trinket 5V 16MHz: Trinket's got a big sister in town - the Pro Trinket 5V! Pro Trinket combines everything you love about Trinket with the familiarity of the common core Arduino chip, the ATmega328. It's like an Arduino Pro Mini with more pins and USB tossed in, so delicious. Trinket's a year old now, and while its been great to see tons of tiny projects, sometimes you just need more pins, more FLASH, and more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
  Neopixel Strip -- Black (30/m): These NeoPixel strips have 30 digitally-addressable pixel LEDs per meter and are very affordable and are only 12.5 mm wide, 10 mm if you remove the strip from the casing.
